# Fritzing sketch Serre Ethernet Arduino 4 chan relay (saved by Fritzing 0.9.4)

parts:
  U2 = Module 4 Relais 5V [package="Module 4 Relais 5V"]
  Composant2 = Arduino Board Ethernet

nets:
  N1: U2.IN1, Composant2.D2_PWM
  N2: U2.IN2, Composant2.D3_PWM
  N3: U2.IN3, Composant2.D4
  N4: U2.IN4, Composant2.D5_PWM
  N5: U2.K4-Com, Composant2.GND
  N6: U2.K1-NO, Composant2.VIN

notes:
  Red : Main +12V
  Black : Main Ground
  Actuator 1
  Actuator 2

custom parts:
  Module 4 Relais 5V: Module 4 Relais 5V 4x SPD-06VDC-SD-C
